# Fritzing sketch skematik (saved by Fritzing 0.9.3b)
circuit board: 8.46667cm x 5.64444cm

parts:
  Part1 = Arduino Nano (Rev3.0)
  Part3 = Logic Level Converter
  U2 = ESP8266 WiFi Module [part_number=ESP8266]
  U3 = V_REG_LD1117VXX [package=78xxl]
  J1 = Power Jack [package=power_jack_combo]
  Part4 = NRF24L01+ Breakout Board
  JP1 = Header 8 [package=1x08_smd_alt]
  JP2 = Header 8 [package=1x08_smd_alt]
  U4 = V_REG_LD1117VXX [package=78xxl]
  J2 = double row female pin header, 2 pins [form="♀ (female)"]
  J3 = double row female pin header, 2 pins [form="♀ (female)"]  # not connected

nets:
  N1: Part1.D1/TX, JP2.5
  N2: Part1.D0/RX, JP2.6
  N3: Part1.RESET, JP2.8
  N4: Part1.GND, J1.GNDBREAK, JP1.8
  N5: Part1.D2, JP2.4
  N6: Part1.D3, JP2.2
  N7: Part1.D9, Part4.CE
  N8: Part1.D10, Part4.CS
  N9: Part1.D11/MOSI, Part4.MOSI
  N10: Part1.D12/MISO, Part4.MISO
  N11: Part1.VIN, J2.pin1
  N12: Part1.D13/SCK, Part4.SCK
  N13: Part3.TX2_LV, JP2.1
  N14: Part3.RX2_LV, JP2.3
  GND: Part3.GND, U2.GND, JP1.7
  N15: Part3.RX2_HV, JP1.2
  N16: Part3.TX2_HV, JP1.4
  N17: U2.RXD, JP1.3, JP1.5
  N18: U2.VCC, U3.OUT
  N19: U2.GPIO_0, JP2.7
  N20: U2.TXD, JP1.1, JP1.6
  N21: J1.PWR, U4.IN
  N22: Part4.VCC, U4.OUT

custom parts:
  ESP8266 WiFi Module: Generic WiFi Module based on the ESP8266 with onboard PCB antenna and UART communications
